# Fritzing sketch ESP32_mqtt_client_hardware (saved by Fritzing 0.9.8b)
breadboards: 1

parts:
  MH-ET_LIVE_ESP32_DEVKIT1 = MH-ET LIVE ESP32 DEVKIT 38 pins
  LED1 = LED - 3mm [color="Red (633nm)" current=0.030 package="3 mm [THT]"]
  LED2 = LED - 3mm [color="Red (633nm)" current=0.030 package="3 mm [THT]"]
  R1 = Resistor [tolerance=±5% power=0.25 resistance=330 package=THT]
  R2 = Resistor [tolerance=±5% power=0.25 resistance=330 package=THT]

nets:
  N1: MH-ET_LIVE_ESP32_DEVKIT1.IO34, LED1.anode
  N2: MH-ET_LIVE_ESP32_DEVKIT1.IO35, LED2.anode
  N3: MH-ET_LIVE_ESP32_DEVKIT1.GND#58, R1.Pin_1, R2.Pin_1
  N4: LED1.cathode, R2.Pin_0
  N5: LED2.cathode, R1.Pin_0

custom parts:
  MH-ET LIVE ESP32 DEVKIT 38 pins: http://mh.nodebb.com/topic/2/mh-et-live-esp32-devkit
